// Logisim project Project 1 - With Extra Credit.circ as structural Verilog: 1 circuit, main circuit main
module main (
  input  A,
  input  B,
  input  C,
  input  D
);

  wire and_1_out, and_2_out, and_3_out, and_4_out, and_5_out, and_6_out, and_7_out, and_8_out, and_9_out,
       not_1_out, not_2_out, not_3_out, or_1_out, or_2_out, or_3_out, or_4_out, or_5_out, or_6_out, or_7_out,
       or_8_out, or_9_out, or_10_out, or_11_out, or_12_out, or_13_out, or_14_out, or_15_out, or_16_out;

  not not_1 (not_1_out, B);
  or or_1 (or_1_out, C, A);
  not not_2 (not_2_out, C);
  and and_1 (and_1_out, not_2_out, B);
  not not_3 (not_3_out, D);
  and and_2 (and_2_out, not_3_out, not_2_out);
  and and_3 (and_3_out, D, C);
  and and_4 (and_4_out, not_3_out, not_1_out);
  and and_5 (and_5_out, D, B);
  and and_6 (and_6_out, not_3_out, C);
  or or_2 (or_2_out, not_3_out, not_2_out);
  or or_3 (or_3_out, not_3_out, not_1_out);
  or or_4 (or_4_out, and_4_out, and_6_out);
  or or_5 (or_5_out, D, B);
  and and_7 (and_7_out, or_2_out, B);
  and and_8 (and_8_out, or_3_out, C);
  and and_9 (and_9_out, and_5_out, not_2_out);
  or or_6 (or_6_out, and_2_out, and_3_out);
  or or_7 (or_7_out, and_4_out, and_5_out);
  or or_8 (or_8_out, and_7_out, A);
  or or_9 (or_9_out, and_8_out, A);
  or or_10 (or_10_out, or_6_out, not_1_out);
  or or_11 (or_11_out, or_7_out, or_1_out);
  or or_12 (or_12_out, and_2_out, or_8_out);
  or or_13 (or_13_out, or_9_out, and_1_out);
  or or_14 (or_14_out, or_9_out, and_4_out);
  or or_15 (or_15_out, or_5_out, not_2_out);
  or or_16 (or_16_out, or_14_out, and_9_out);
  _7_Segment_Display u_7_segment_display_1 (
    .g(or_13_out), .f(or_12_out), .a(or_11_out), .b(or_10_out), .e(or_4_out), .d(or_16_out), .c(or_15_out));  // open: dp

  // Notes on the sheet:
  //   b = B' + CD + C'D'
  //   a = A + C + BD + B'D'
  //   f = A + BC' + BD' + C'D'
  //   g = A + B'C + CD' + BC'
  //   e = B'D' + CD'
  //   d = A + B'C + CD' + B'D' + BC'D
  //   c = B + D + C'
endmodule
